# Fritzing sketch board (saved by Fritzing 0.9.3b)
circuit board: 7.17674cm x 5.58416cm
breadboards: 1

parts:
  part = Arduino Uno (Rev3) [part_number=LUNEX]
  J1 = Screw terminal - 2 pins [package=THT]
  J2 = Screw terminal - 2 pins [package=THT]
  J3 = Screw terminal - 2 pins [package=THT]
  J4 = Screw terminal - 2 pins [package=THT]
  J5 = Screw terminal - 2 pins [package=THT]
  J6 = Screw terminal - 2 pins [package=THT]
  J8 = Screw terminal - 2 pins [package=THT]
  J9 = Screw terminal - 2 pins [package=THT]
  J10 = Screw terminal - 2 pins [package=THT]
  J11 = Screw terminal - 2 pins [package=THT]
  J12 = Screw terminal - 2 pins [package=THT]
  R1 = Resistor [tolerance=±5% resistance=330 package=THT]
  LED1 = LED - 3mm [color="Green (565nm)" package="3 mm [THT]"]
  J7 = Screw terminal - 2 pins [package=THT]
  J13 = Screw terminal - 2 pins [package=THT]

nets:
  N1: part.D8, J8.pin1
  N2: part.D9_PWM, J11.pin1
  N3: part.D10_PWM/SS, J7.pin2
  N4: part.D11_PWM/MOSI, J2.pin2
  N5: part.D12/MISO, J3.pin1
  N6: part.GND, J1.pin2, J3.pin2, J5.pin2, J6.pin1, J9.pin1, J10.pin2, LED1.cathode, J13.pin1
  N7: part.D2, J11.pin2
  N8: part.D3_PWM, J7.pin1
  N9: part.D4, R1.Pin_1
  N10: part.D5_PWM, J4.pin2, J5.pin1
  N11: part.D7, J12.pin2
  N12: part.5V, J1.pin1, J2.pin1, J4.pin1
  N13: J6.pin2, J9.pin2, J10.pin1, J13.pin2
  N14: R1.Pin_0, LED1.anode

notes:
  +5V
  0V
  Trig
  Echo
  Puls
  OV
  12V
  FG
  PWM
  DIR
  NOIR
  ROUGE
  JAUNE
  BLANC
  BLEU
  RIGHT
  LEFT
  HC-SR04
  LUNEX
  MOTOR & SENSOR
  FAN
  C. Jiwan
